# Fritzing sketch RemoteFeeder (saved by Fritzing 0.9.0b)
breadboards: 3

parts:
  U7 = atmega328 [package=dip]
  CD4021B3 = CD4021B - Shift Register [part_number=893806 package="DIP16 [THT]"]  # not connected
  IC6 = L293D [package=THT]  # not connected
  IC7 = L293D [package=THT]  # not connected
  IC8 = IC, DIP package, 14 pins [chip_label=SN74HC04N]
  C14 = Electrolytic Capacitor [capacitance=10µF rated_voltage=35V package="100 mil [THT, electrolytic]"]
  C15 = Electrolytic Capacitor [capacitance=10µF rated_voltage=35V package="100 mil [THT, electrolytic]"]
  U8 = Voltage Regulator - 5V [package="TO220 [THT]"]
  Power_plug4 = Power plug
  R20 = Resistor [tolerance=±5% resistance=1k package=THT]
  X3 = DB9 Connector [package=db9]
  C16 = Ceramic Capacitor [capacitance=0.1µF package="100 mil [THT, multilayer]"]

nets:
  N1: U7.RESET, R20.Pin_1, C16.1
  N2: U7.D0_(RX), IC8.pin2
  N3: U7.D1_(TX), IC8.pin3
  N4: U7.AVCC, U7.AREF, IC8.pin14, R20.Pin_0
  N5: U7.GND#21, IC8.pin7, X3.9
  N6: IC8.pin1, X3.7
  N7: IC8.pin4, X3.6
  N8: C14.-, Power_plug4.GND
  N9: C14.+, U8.input_voltage, Power_plug4.VCC
  N10: C15.-, C15.+, U8.output_voltage
  N11: X3.8, C16.0

custom parts:
  CD4021B - Shift Register: Shift Register Single 8 Bit Serial Parallel To Parallel 16 Pin Plastic DIP Tube
